# Fritzing sketch pcb (saved by Fritzing 0.9.10b)
circuit board: 5cm x 5cm
breadboards: 1

parts:
  Arduino_Nano = Arduino Nano (Rev3.0) (ICSP)
  R1 = Resistor [tolerance=±5% power=0.25 resistance=4.7k package=THT]
  J1 = female pin header, 3 pins [form="♀ (female)"]
  J2 = female pin header, 3 pins [form="♀ (female)"]
  J3 = female pin header, 4 pins [form="♀ (female)"]
  J4 = female pin header, 3 pins [form="♀ (female)"]
  Temperature_Inside = LM35 Temperature Sensor [package="TO92 [THT]"]
  Temperature_Outside = LM35 Temperature Sensor [package="TO92 [THT]"]
  OLED = Grove OLED 128x96

nets:
  N1: Arduino_Nano.D2, R1.Pin_1, J1.pin1, J2.pin1, Temperature_Inside.+Vs, Temperature_Outside.+Vs
  N2: Arduino_Nano.D3, J4.pin1
  GND: Arduino_Nano.GND, J1.pin3, J2.pin3, J3.pin4, J4.pin3, Temperature_Inside.GND, Temperature_Outside.GND, OLED.GND
  N3: Arduino_Nano.5V, J4.pin2
  N4: Arduino_Nano.A5, J3.pin2, OLED.SDA
  N5: Arduino_Nano.A4, J3.pin1, OLED.SCL
  3V3: Arduino_Nano.3V3, R1.Pin_0, J1.pin2, J2.pin2, J3.pin3, Temperature_Inside.Vout, Temperature_Outside.Vout, OLED.VCC
